# Fritzing sketch pottySense (saved by Fritzing 1.0.4)
breadboards: 2

parts:
  A1 = Particle - Photon2
  Disp1 = 20mm 8x8 dot matrix column cathode led display with standard pcb pads
  Part1 = 12 NeoPixel Ring [part_number=1643]
  LD1 = LD
  S1 = Pushbutton [package="[THT]"]
  Water_Level_Sensor1 = Water Level Sensor
  OLED_I2C1 = OLED 128x64 I2C Monochrome Display
  LED1 = LEDs [package=led10mm]

nets:
  VCC: A1.Pin_2, S1.Pin_3, S1.Pin_4, Water_Level_Sensor1.VCC, OLED_I2C1.VDD, LED1.A
  GND: A1.Pin_4, A1.Pin_30, Disp1.pin_10, Part1.GND, LD1.cathode, Water_Level_Sensor1.GND, OLED_I2C1.GND
  N1: A1.Pin_11, Water_Level_Sensor1.SIG
  N2: A1.Pin_12, LED1.C
  N3: A1.Pin_17, OLED_I2C1.SDA
  N4: A1.Pin_18, OLED_I2C1.SCK
  N5: A1.Pin_19, Disp1.pin_15
  N6: A1.Pin_20, LD1.anode
  N7: A1.Pin_21, S1.Pin_1, S1.Pin_2
  N8: A1.Pin_26, Disp1.pin_14, Part1.VDD
  N9: Disp1.pin_2, Part1.IN

custom parts:
  Particle - Photon2: The Photon 2 is a microcontroller and Wi-Fi networking developed by particle. Features: 802.11a/b/g/n Wi-Fi, 2.4 GHz and 5 GHz Integrated PCB antenna Integrated U.FL connector for external antenna Integrated RF switch BLE 5 using same antenna as Wi-Fi Realtek RTL8721DM MCU ARM Cortex M33 CPU, 200 MHz 2048 KB (2 MB) user application maximum size 3072 KB (3 MB) of RAM available to user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
  12 NeoPixel Ring: 12 ultra bright smart LED NeoPixels are arranged in a circle with 1.5" (37mm) outer diameter. The rings are 'chainable' - connect the output pin of one to the input pin of another. Use only one microcontroller pin to control as many as you can chain together! Each LED is addressable as the driver chip is inside the LED. Each one has ~18mA constant current drive so the color will be very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
  LD: A Generic Red Dot Laser Diode Module (~5mW)
  Pushbutton: A generic pushbutton.
  Water Level Sensor: A water level sensor. This sensor operates at 3V to 5V. The Sig (signal) pin outputs an analogue signal that is in proportion to the amount of water in contact with the sensor.
